// Logisim project 202169930.circ as structural Verilog: 1 circuit, main circuit main
module main (
  input  in_1,
  input  in_2,
  input  in_3,
  input  in_4,
  input  in_5,
  input  in_6,
  input  in_7,
  input  in_8,
  input  in_9,
  input  in_10,
  input  [2:0] in_11,
  input  in_12,
  input  in_13,
  input  [2:0] in_14,
  output out_15,
  output out_16,
  output out_17,
  output out_18,
  output out_19,
  output out_20
);

  wire and_1_out, and_2_out, and_3_out, and_4_out, decoder_1_out1, decoder_1_out2, decoder_1_out4,
       decoder_1_out7, decoder_2_out0, decoder_2_out3, decoder_2_out5, decoder_2_out6, nand_1_out,
       nand_2_out, nand_3_out, nand_4_out, not_1_out, not_2_out, not_3_out, not_4_out, not_5_out, not_6_out,
       xor_2_out;

  not not_1 (not_1_out, in_10);
  not not_2 (not_2_out, in_12);
  not not_3 (not_3_out, in_13);
  xor xor_1 (out_15, in_1, in_3, in_4);
  xor xor_2 (xor_2_out, in_6, in_8);
  and and_1 (and_1_out, not_1_out, not_2_out, in_13);
  and and_2 (and_2_out, not_1_out, in_12, not_3_out);
  and and_3 (and_3_out, in_10, not_2_out, not_3_out);
  and and_4 (and_4_out, in_10, in_12, in_13);
  xor xor_3 (out_17, xor_2_out, in_9);
  or or_1 (out_19, and_1_out, and_2_out, and_3_out, and_4_out);
  not not_4 (not_4_out, in_2);
  not not_5 (not_5_out, in_5);
  not not_6 (not_6_out, in_7);
  Decoder #(.select(3)) decoder_1 (
    .out1(decoder_1_out1), .out2(decoder_1_out2), .out4(decoder_1_out4), .out7(decoder_1_out7), .sel(in_11));  // open: out0, out3, out5, out6, en
  Decoder #(.select(3)) decoder_2 (
    .out0(decoder_2_out0), .out3(decoder_2_out3), .out5(decoder_2_out5), .out6(decoder_2_out6), .sel(in_14));  // open: out1, out2, out4, out7, en
  nand nand_1 (nand_1_out, not_4_out, not_5_out, in_7);
  nand nand_2 (nand_2_out, not_4_out, in_5, not_6_out);
  nand nand_3 (nand_3_out, in_2, not_5_out, not_6_out);
  nand nand_4 (nand_4_out, in_2, in_5, in_7);
  or or_2 (out_18, decoder_1_out1, decoder_1_out2, decoder_1_out4, decoder_1_out7);
  nand nand_5 (out_16, nand_1_out, nand_2_out, nand_3_out, nand_4_out);
  nor nor_1 (out_20, decoder_2_out0, decoder_2_out3, decoder_2_out5, decoder_2_out6);
endmodule
